# Fritzing sketch Blynk_Relay_control (saved by Fritzing 0.9.3b)
breadboards: 1

parts:
  U1 = NodeMCU V1.0
  R1 = Resistor [tolerance=±5% resistance=220 package=THT]
  LED1 = LED - 5mm [color="Red (633nm)" package="5 mm [THT]"]
  KY-1 = Keyes Relay [package=THT]
  KY-2 = Keyes Relay [package=THT]

nets:
  N1: U1.D0, R1.Pin_1
  N2: U1.D1, KY-1.ground
  N3: U1.D2, KY-2.ground
  N4: U1.GND, LED1.cathode, KY-1.power, KY-2.power
  N5: U1.Vin, KY-1.signal, KY-2.signal
  N6: R1.Pin_0, LED1.anode

custom parts:
  NodeMCU V1.0: ESP8266 based NodeMCU
  Keyes Relay: The Keyes 5V relay module is suitable for SCM development, home appliance control. It uses a 5V~12V TIL control signal which can control DC / AC signal.
